# Fritzing sketch rpi-ballotbox (saved by Fritzing 0.9.2b)
circuit board: 4.11458cm x 3.74969cm
circuit board: 9.24443cm x 7.43725cm
breadboards: 3

parts:
  Switching_regulator = Voltage Regulator - 5V [part_number=PT78ST105H package="TO220 [THT]"]
  LM293D = L293D [package=THT]
  D1 = Rectifier Diode [part_number=1N4001 package="300 mil [THT]"]
  D2 = Rectifier Diode [part_number=1N4001 package="300 mil [THT]"]
  D3 = Rectifier Diode [part_number=1N4001 package="300 mil [THT]"]
  D4 = Rectifier Diode [part_number=1N4001 package="300 mil [THT]"]
  2A = Fuse with Handler [part_number=Htc-15m]
  Power_button = Pushbutton [package=THT]
  Feed_motor_sensor = PHOTOTRANSISTOR REFLECTIVE OBJECT SENSOR [part_number="HP J110a" package=qrb1114-side]
  R1 = Resistor [tolerance=±5% resistance=220 package=THT]
  R2 = Resistor [tolerance=±5% resistance=7.5k package=THT]
  Diverter_servo = Basic Servo [part_number="Futaba S3003"]
  Paper_sensor = PHOTOTRANSISTOR REFLECTIVE OBJECT SENSOR [package=qrb1114-side]
  Raspberry_Pi2 = Raspberry Pi 2
  R3 = Resistor [tolerance=±5% resistance=220 package=THT]
  R4 = Resistor [tolerance=±5% resistance=1k package=THT]
  Q1 = NPN-Transistor [part_number=2N2222A package="TO92 [THT]"]
  R5 = Resistor [tolerance=±5% resistance=120k package=THT]
  Scanner_switch = male pin header, 2 pins [form="♂ (male)"]
  Sheet_feeder = DC Motor [part_number="HP J110a"]
  12Vdc_adapter = Power Jack [package=power_jack_pth_lock]
  C1 = Electrolytic Capacitor [capacitance=0.1mF package="100 mil [THT, electrolytic]"]
  C2 = Electrolytic Capacitor [capacitance=1µF package="100 mil [THT, electrolytic]"]
  Paper_sensor_socket = male pin header, 3 pins [form="♂ (male)"]
  Feed_sensor_socket = male pin header, 3 pins [form="♂ (male)"]
  Pad5V = Pad [width=7 height=4 connect=center]
  PadGnd = Pad [width=7 height=4 connect=center]
  Pad12V = Pad [width=7 height=4 connect=center]
  Pad3V3 = Pad [width=7 height=4 connect=center]
  LM386 = LM386 [part_number=LM386 package=dip08]
  Audio_jack = Audio Jack (TRS) 3.5mm [package="PG203J [THT]"]
  R6 = Resistor [tolerance=±5% resistance=10 package=THT]
  R7 = Resistor [tolerance=±5% resistance=22 package=THT]
  C3 = Electrolytic Capacitor [capacitance=330µF package="100 mil [THT, electrolytic]"]
  C4 = Tantalum Capacitor [capacitance=10µF package="100 mil [THT, tantalum]"]
  R8 = Rotary Potentiometer (Large) [maximum_resistance=10kΩ package=THT]
  SP1 = SPEAKER [package=pcb_mount_speaker]
  C5 = Ceramic Capacitor [capacitance=50nF package="100 mil [THT, multilayer]"]
  J1 = male pin header, 2 pins [form="♂ (male)"]
  J2 = male pin header, 2 pins [form="♂ (male)"]

nets:
  N1: Switching_regulator.input_voltage, 2A.Connector2, C2.+
  GND: Switching_regulator.GND, LM293D.0V, D3.anode, D4.anode, Power_button.leg1, Feed_motor_sensor.E, Feed_motor_sensor.K, Diverter_servo.gnd, Raspberry_Pi2.GND, R3.Pin_0, R4.Pin_0, 12Vdc_adapter.GND, 12Vdc_adapter.GNDBREAK, C1.-, C2.-, Feed_sensor_socket.pin2, PadGnd.pad, LM386.-IN, LM386.V-, Audio_jack.Sleeve, R8.leg1, SP1.-, C5.0, J1.pin2, J2.pin1
  VCC: Switching_regulator.output_voltage, LM293D.+V, Diverter_servo.vcc, Raspberry_Pi2.5V, C1.+, Pad5V.pad
  N2: LM293D.Enable_1, Raspberry_Pi2.GPIO17
  N3: LM293D.In_1, Raspberry_Pi2.GPIO27
  N4: LM293D.Out_1_(_Controlled_by_Enable_1_), D2.anode, D4.cathode, Sheet_feeder.pin_2
  N5: LM293D.Out_2_(_Controlled_by_Enable_1_), D1.anode, D3.cathode, Sheet_feeder.pin_1
  N6: LM293D.In_2, Raspberry_Pi2.GPIO22
  N7: LM293D.+Vmotor, D1.cathode, D2.cathode, 2A.Connector1, 12Vdc_adapter.PWR, Pad12V.pad, LM386.V+, J2.pin2
  N8: Power_button.leg0, Raspberry_Pi2.GPIO3
  N9: Feed_motor_sensor.A, R1.Pin_1, Feed_sensor_socket.pin1
  N10: Feed_motor_sensor.C, R2.Pin_1, Raspberry_Pi2.GPIO23, Feed_sensor_socket.pin3
  3V3: R1.Pin_0, R2.Pin_0, Paper_sensor.A, Paper_sensor.C, Raspberry_Pi2.3v3, Raspberry_Pi2.3V3, Paper_sensor_socket.pin3, Pad3V3.pad
  N11: Diverter_servo.pulse, Raspberry_Pi2.GPIO18
  N12: Paper_sensor.E, Raspberry_Pi2.GPIO24, R4.Pin_1, Paper_sensor_socket.pin2
  N13: Paper_sensor.K, R3.Pin_1, Paper_sensor_socket.pin1
  N14: Raspberry_Pi2.GPIO25, R5.Pin_0
  N15: Q1.E, Scanner_switch.pin2
  N16: Q1.B, R5.Pin_1
  N17: Q1.C, Scanner_switch.pin1
  N18: LM386.GAIN, R7.Pin_0, C4.-
  N19: LM386.+IN, R8.wiper
  N20: LM386.OUT, R6.Pin_0, C3.+
  N21: Audio_jack.Tip, R8.leg2
  N22: R6.Pin_1, C5.1
  N23: R7.Pin_1, C4.+
  N24: C3.-, SP1.+, J1.pin1

notes:
  GPIO17
  GPIO27
  GPIO22
  GPIO18
  5V
  GPIO3
  GPIO25
  Paper_sens
  Feed_sens
  Motor
  12V
  PWR
  SCAN
  SERVO
  5VREG
  RPI_GPIO
  1
  16
  +
  Gnd
  SVote2 Rev. 1.01
  3V3
  Blk
  Grn
  Yel
  SIG
  Note: this is not the correct pinout for 3.5mm that we have!
  SPKR
  VOLUME
  3.5MM
